# Fritzing sketch lightsControl-connections (saved by Fritzing 0.9.3b)
breadboards: 1

parts:
  LED1 = RGB LED (com. cathode, rgb) [package="5 mm [THT]"]
  R5 = Resistor [tolerance=±5% resistance=330 package=THT]
  LED2 = LED - 5mm [color="White (6500K)" package="5 mm [THT]"]
  LED3 = LED - 5mm [color="Yellow (595nm)" package="5 mm [THT]"]
  S1 = Pushbutton [package="[THT]"]
  S2 = Pushbutton [package="[THT]"]
  S3 = Pushbutton [package="[THT]"]
  Componente3 = Arduino Mega 2560 (Rev3)
  U1 = LUXEON-REBEL [package=luxeon-rebel]
  Componente2 = Bluetooth HC-05 Macho

nets:
  N1: LED1.red_anode, Componente3.D5_PWM
  N2: LED1.common_cathode, R5.Pin_0
  N3: LED1.green_anode, Componente3.D4_PWM
  N4: LED1.blue_anode, Componente3.D3_PWM
  N5: R5.Pin_1, Componente3.5V, U1.A
  N6: LED2.cathode, Componente3.D2_PWM
  GND: LED3.cathode, S1.Pin_1, S1.Pin_2, S2.Pin_1, S2.Pin_2, S3.Pin_1, S3.Pin_2, Componente3.GND, U1.S, Componente2.GND
  N7: LED3.anode, Componente3.D53
  N8: S1.Pin_3, S1.Pin_4, Componente3.D50
  N9: S2.Pin_3, S2.Pin_4, Componente3.D51
  N10: S3.Pin_3, S3.Pin_4, Componente3.D52
  N11: Componente3.A7, U1.C
  N12: Componente3.D19/RX1, Componente2.TXD
  N13: Componente3.D18/TX1, Componente2.RXD
  N14: Componente3.D32, Componente2.VCC
  N15: Componente3.D33, Componente2.Key

// code stored in the sketch: lightsControl.ino

//+ to "button" level
//BUTTON_PIN to "button"
//"resistor" to BUTTON_PIN
//"resistor" to -

//- to "resistor"
// "resistor" to light
//LIGHT_PIN to light

//"lightSensor" to +
//"lightSensor" to -
//"lightSensor" to LIGHT_SENSOR_PIN

const bool BT_ENABLED = true; //bluetooth
const bool LS_ENABLED = true; //light sensor

const int LIGHT_SENSOR_PIN = A7;//analog in
const int LIGHT_PIN_W = 2;//PWM pin
const int LIGHT_PIN_R = 3;//PWM pin
const int LIGHT_PIN_G = 4;//PWM pin
const int LIGHT_PIN_B = 5;//PWM pin
const int LS_LED_PIN = 53;//auto enabled indicator
const int LEVEL_BUTTON_PIN =  52;
const int COLOR_BUTTON_PIN =  51;
const int AUTO_BUTTON_PIN = 50;

//lightSensor
unsigned long lastLSensorCheck = 0;//light sensor timer
const int lightSensorCheckTime = 2000;

//button
unsigned long buttonLastPressed = 0;//buttons timer
const int BUTTON_MIN_TIME = 150;

bool levelChanged;
bool colorChanged;
bool automaticLevel;

int currentLevel = 0;
int currentColor = 0;
int targetLevel = 0;
int targetColor = 0;
const int MAX_LEVEL = 3;
const int MAX_COLOR = 3;

int lightsPin[4] = {LIGHT_PIN_W,
                  LIGHT_PIN_R,
                  LIGHT_PIN_G,
                  LIGHT_PIN_B};
const int WHITE = 0;
const int RED = 1;
const int GREEN = 2;
const int BLUE = 3;

void setup() 
{
  for(int i=0; i<= MAX_COLOR; i++)
  {
    pinMode(lightsPin[i], OUTPUT);
  }

  pinMode(COLOR_BUTTON_PIN, INPUT);
  pinMode(LEVEL_BUTTON_PIN, INPUT);
  pinMode(AUTO_BUTTON_PIN, INPUT);
  pinMode(LS_LED_PIN, OUTPUT);

  Serial.begin(9600);
  if(BT_ENABLED)
  {
    Serial1.begin(9600);
  }

  testLights();

  automaticLevel = false;
}

void testLights()
{
  for(int i=0; i<=MAX_COLOR; i++)
  {
    for(int j=MAX_LEVEL; j<=0; j--)
    { 
      updateLigts(j,i);
      delay(500);
    }
  }

  //test autoLevel indicator led
  digitalWrite(LS_LED_PIN, HIGH);
  delay(500);
  digitalWrite(LS_LED_PIN, LOW);
  delay(500);
}

void loop() 
{
  digitalWrite(LS_LED_PIN, automaticLevel);
  //read level from button
  readLevelButton();
  //read color fromm button
  readColorButton();

  //read level from light sensor
  readLightSensor();

  //check active auto level
  readAutomaticButton();

  //read mode from bluetooh
  readBluetooth();

  levelChanged = currentLevel != targetLevel;
  colorChanged = currentColor != targetColor;
  if(levelChanged || colorChanged)
  {
    currentLevel = targetLevel;
    currentColor = targetColor;
    updateLigts(currentLevel, currentColor);
  }
}

int getLightValueByLevel(int level)
{
  if(level == 0)
  {
    return 0;
  }
  else
  {
    return level * 75 + 30;
  }
}

void updateLigts(int currentLevel, int currentColor)
{
  for(int i=0; i<=MAX_COLOR; i++)
  {
    if(i == currentColor)
    {
      analogWrite(lightsPin[i], getLightValueByLevel(currentLevel));
    }
    else
    {
      analogWrite(lightsPin[i], 0);
    }
  }
}

void readLevelButton()
{
  if(digitalRead(LEVEL_BUTTON_PIN) == HIGH)
  {
    if(millis() - buttonLastPressed >= BUTTON_MIN_TIME)
    {
      Serial.print("Level button pressed");
      setAutomaticEnable(false);
      targetLevel = currentLevel + 1;
      if(targetLevel > MAX_LEVEL)
      {
        targetLevel = 0;
      }
    }
    buttonLastPressed = millis();
  }
}

void readColorButton()
{
  if(digitalRead(COLOR_BUTTON_PIN) == HIGH)
  {
    if(millis() - buttonLastPressed >= BUTTON_MIN_TIME)
    {
      Serial.print("Color button pressed");
      
      targetColor = currentColor + 1;
      if(targetColor > MAX_COLOR)
      {
        targetColor = 0;
      }
    }
    buttonLastPressed = millis();
  }
}

void readAutomaticButton()
{
  if(digitalRead(AUTO_BUTTON_PIN) == HIGH)
  {
    Serial.print("AutoLevel button pressed");
    if(millis() - buttonLastPressed >= BUTTON_MIN_TIME)
    {
      setAutomaticEnable(!automaticLevel);
    }
    buttonLastPressed = millis();
  }
}

void readBluetooth()
{
  if(BT_ENABLED && Serial1.available() > 0)
  {
    char data = Serial1.read();
    switch(data)
    {
      case '0':
        targetLevel = 0;
        break;
      case '1':
        targetLevel = 1;
        break;
      case '2':
        targetLevel = 2;
        break;
      case '3':
        targetLevel = 3;
        break;
      case 'a':
        automaticLevel = !automaticLevel;
        break;
      case 'w':
        targetColor = WHITE;
        break;
      case 'r':
        targetColor = RED;
        break;
      case 'g':
        targetColor = GREEN;
        break;
      case 'b':
        targetColor = BLUE;
        break;
      default:
        break;
    }
  }
}

void setAutomaticEnable(bool value)
{
  automaticLevel = value;
}

void readLightSensor()
{
  if(LS_ENABLED && automaticLevel)
  {
    if(millis() -lastLSensorCheck > lightSensorCheckTime)
    {
      int data =  analogRead(LIGHT_SENSOR_PIN);
      //Serial.print("Read from light sensor: " + data + " of 1024");
      Serial.print("\n");
      
      if(data >= 300)
      {
        //level 0
        targetLevel = 0;
      }
      else if(data >= 40)
      {
        //level 1
        targetLevel = 1;
      }
      else if(data >= 25)
      {
        //level 2
        targetLevel = 2;
      }
      else
      {
        //level 3
        targetLevel = 3;
      }
      
      //update light sensor timer
      lastLSensorCheck = millis();
    }
  }
}
